# Fritzing sketch CPR Demo (saved by Fritzing 0.9.3b)
circuit board: 8.46667cm x 5.64444cm
breadboards: 1

parts:
  CPR_Demo_Sketch = Arduino Uno (Rev3)
  Beats_Pot_-_R1 = Slide Potentiometer [maximum_resistance=20kΩ]
  S1_START/STOP = Square Pushbutton
  S2_ADULT/CHILD = Square Pushbutton
  R3 = Resistor [tolerance=±5% resistance=220 package="0402 [SMD]"]
  R4 = Resistor [tolerance=±5% resistance=220 package="0402 [SMD]"]
  ADULT/CHILD = LED - 3mm [color="Yellow (574nm)" package="3 mm [THT]"]
  START/STOP = smd LED [color="Green (560nm)" package="1206 [SMD]"]
  Time_Pot_-_R2 = Rotary Potentiometer (Large) [maximum_resistance=50kΩ package=THT]
  Red_Display = Seven-Segment LED Backpack 1.2 Inch Digits [part_number=1270]
  Green_Display = Seven-Segment LED Backpack 1.2 Inch Digits [part_number=1268]
  Audio_Client_Sketch = Arduino Uno (Rev3)
  V1 = DC Power [voltage=12V]
  AVERAGE_BPM = smd LED [color="Green (560nm)" package="1206 [SMD]"]
  OVERALL_BPM = smd LED [color="Green (560nm)" package="1206 [SMD]"]
  R5 = Resistor [tolerance=±5% resistance=220 package="0402 [SMD]"]
  R6 = Resistor [tolerance=±5% resistance=220 package="0402 [SMD]"]
  U5 = Neopixel Stick - 8 pins [chip_label="Neopixel Stick" package=THT]
  U3 = Neopixel Stick - 8 pins [chip_label="Neopixel Stick" package=THT]
  U4 = Neopixel Stick - 8 pins [chip_label="Neopixel Stick" package=THT]

nets:
  N1: CPR_Demo_Sketch.A0, Time_Pot_-_R2.wiper
  N2: CPR_Demo_Sketch.A1, Beats_Pot_-_R1.wiper
  N3: CPR_Demo_Sketch.A4/SDA, Red_Display.SDA, Green_Display.SDA
  N4: CPR_Demo_Sketch.D8, R3.Pin_0
  N5: CPR_Demo_Sketch.D9_PWM, R5.Pin_0
  N6: CPR_Demo_Sketch.D10_PWM/SS, R6.Pin_0
  N7: CPR_Demo_Sketch.D12/MISO, R4.Pin_0
  GND: CPR_Demo_Sketch.GND, S1_START/STOP.leg1, S2_ADULT/CHILD.leg1, ADULT/CHILD.cathode, START/STOP.cathode, Red_Display.GND, Green_Display.GND, Audio_Client_Sketch.GND, V1.V-, AVERAGE_BPM.cathode, OVERALL_BPM.cathode, U3.Gnd#3
  N8: CPR_Demo_Sketch.A5/SCL, Red_Display.SCL, Green_Display.SCL
  N9: CPR_Demo_Sketch.D0/RX, Audio_Client_Sketch.D1/TX
  N10: CPR_Demo_Sketch.D1/TX, Audio_Client_Sketch.D0/RX
  N11: CPR_Demo_Sketch.D2, S1_START/STOP.leg0
  N12: CPR_Demo_Sketch.D4, S2_ADULT/CHILD.leg0
  N13: CPR_Demo_Sketch.D6_PWM, U3.Data_In
  VDD: CPR_Demo_Sketch.5V, Beats_Pot_-_R1.leg2, Time_Pot_-_R2.leg2, Red_Display.VDD, Red_Display.VCCIO, Green_Display.VDD, Green_Display.VCCIO, U3.Vcc#0
  N14: CPR_Demo_Sketch.VIN, V1.V+
  N15: Beats_Pot_-_R1.leg1, Time_Pot_-_R2.leg1
  N16: R3.Pin_1, START/STOP.anode
  N17: R4.Pin_1, ADULT/CHILD.anode
  N18: AVERAGE_BPM.anode, R5.Pin_1
  N19: OVERALL_BPM.anode, R6.Pin_1
  N20: U5.Vcc, U4.Vcc#7
  N21: U5.Data_In, U4.Data_Out
  N22: U5.Gnd, U4.Gnd#4
  N23: U3.Gnd#4, U4.Gnd#3
  N24: U3.Data_Out, U4.Data_In
  N25: U3.Vcc#7, U4.Vcc#0

custom parts:
  Seven-Segment LED Backpack 1.2 Inch Digits: This jumbo 1.2" 7-segment LED display includes a driver chip for simple control via an I2C interface. The backpack features address-selection jumpers so you can connect up to eight displays on a single I2C bus.
  Seven-Segment LED Backpack 1.2 Inch Digits: This jumbo 1.2" 7-segment LED display includes a driver chip for simple control via an I2C interface. The backpack features address-selection jumpers so you can connect up to eight displays on a single I2C bus.
  Neopixel Stick - 8 pins: Adafruit Neopixel Stick
